# Fritzing sketch circuit (saved by Fritzing 0.9.3b)
breadboards: 2

parts:
  U1 = ESP8266 WiFi Module [part_number=ESP8266]
  S3 = Toggle Switch [package=THT]
  J1 = female pin header, 2 pins [form="♀ (female)"]
  J2 = female pin header, 2 pins [form="♀ (female)"]
  RESET = Pushbutton [package="[THT]"]
  MODE = Pushbutton [package="[THT]"]
  BRIGHTNESS = Pushbutton [package="[THT]"]
  Part1 = Adafruit DS3231 [part_number="Adafruit #3013"]
  RGB_SMD_LED1 = SMD RGB LED (WS2812) [package=5050]
  RGB_SMD_LED2 = SMD RGB LED (WS2812) [package=5050]
  RGB_SMD_LED3 = SMD RGB LED (WS2812) [package=5050]
  RGB_SMD_LED4 = SMD RGB LED (WS2812) [package=5050]
  RGB_SMD_LED5 = SMD RGB LED (WS2812) [package=5050]
  RGB_SMD_LED6 = SMD RGB LED (WS2812) [package=5050]
  RGB_SMD_LED7 = SMD RGB LED (WS2812) [package=5050]
  RGB_SMD_LED8 = SMD RGB LED (WS2812) [package=5050]
  RGB_SMD_LED9 = SMD RGB LED (WS2812) [package=5050]
  HLK-PM1 = HLK-PM01
  U2 = Voltage Regulator - 3.3V [package="TO220 [THT]"]
  C1 = Electrolytic Capacitor [capacitance=100µF package="200 mil [THT, electrolytic]"]

nets:
  N1: U1.RXD, J1.pin1
  VCC: U1.VCC, U1.GPIO_2, U1.CH_PD, Part1.Vin, U2.output_voltage, C1.+
  N2: U1.GPIO_0, S3.COM
  VSS: U1.GND, U1.GPIO_15, U1.GPIO_12, U1.GPIO_13, U1.REST, S3.L1, J2.pin1, RESET.Pin_1, RESET.Pin_2, RESET.Pin_3, RESET.Pin_4, MODE.Pin_1, MODE.Pin_2, MODE.Pin_3, MODE.Pin_4, BRIGHTNESS.Pin_1, BRIGHTNESS.Pin_2, BRIGHTNESS.Pin_3, BRIGHTNESS.Pin_4, Part1.GND, RGB_SMD_LED1.VSS, RGB_SMD_LED2.VSS, RGB_SMD_LED3.VSS, RGB_SMD_LED4.VSS, RGB_SMD_LED5.VSS, RGB_SMD_LED6.VSS, RGB_SMD_LED7.VSS, RGB_SMD_LED8.VSS, RGB_SMD_LED9.VSS, HLK-PM1.-Vo, U2.GND, C1.-
  N3: U1.TXD, J1.pin2
  N4: U1.GPIO_4, Part1.SDA
  N5: U1.GPIO_5, Part1.SCL
  N6: U1.GPIO_14, RGB_SMD_LED1.DIn
  N7: RGB_SMD_LED1.DOut, RGB_SMD_LED2.DIn
  VDD: RGB_SMD_LED1.VDD, RGB_SMD_LED2.VDD, RGB_SMD_LED3.VDD, RGB_SMD_LED4.VDD, RGB_SMD_LED5.VDD, RGB_SMD_LED6.VDD, RGB_SMD_LED7.VDD, RGB_SMD_LED8.VDD, RGB_SMD_LED9.VDD, HLK-PM1.+Vo, U2.input_voltage
  N8: RGB_SMD_LED2.DOut, RGB_SMD_LED3.DIn
  N9: RGB_SMD_LED3.DOut, RGB_SMD_LED4.DIn
  N10: RGB_SMD_LED4.DOut, RGB_SMD_LED5.DIn
  N11: RGB_SMD_LED5.DOut, RGB_SMD_LED6.DIn
  N12: RGB_SMD_LED6.DOut, RGB_SMD_LED7.DIn
  N13: RGB_SMD_LED7.DOut, RGB_SMD_LED8.DIn
  N14: RGB_SMD_LED8.DOut, RGB_SMD_LED9.DIn

custom parts:
  Adafruit DS3231: The datasheet for the DS3231 explains that this part is an "Extremely Accurate I²C-Integrated RTC/TCXO/Crystal". And, hey, it does exactly what it says on the tin! This Real Time Clock (RTC) is the most precise you can get in a small, low power package. Most RTCs use an external 32kHz timing crystal that is used to keep time with low current draw. And that's all well and good, but those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
